# Fritzing sketch Stapp (saved by Fritzing 0.9.3b)
breadboards: 1

parts:
  Part1 = BME280 Breakout
  U2 = ADXL345 [package=lga14]
  U4 = GP-2106 [package=gp-2106]
  U6 = microSD Socket [package=usd-socket-pp]  # not connected
  VCC1 = Battery block 9V
  U7 = Voltage Regulator LM1117 [package=sot223]  # not connected
  U8 = V_REG MIC5219 [package=sot23-5]
  U1 = ATMEGA2560 [package=tqfp]

nets:
  GND: Part1.GND, U2.GND, U4.GND, VCC1.-, U8.GND, U1.GND3
  N1: VCC1.+, U8.IN
  N2: U8.OUT, U1.VCC2
